# Fritzing sketch Wiring (saved by Fritzing 0.9.9b)
breadboards: 1

parts:
  Part1 = Arduino Uno (Rev3)
  S1 = Pushbutton [package="[THT]"]
  S2 = Pushbutton [package="[THT]"]
  S3 = Pushbutton [package="[THT]"]
  Part2 = Thumb Joystick

nets:
  N1: Part1.A0, Part2.HORZ
  N2: Part1.A1, Part2.VERT
  N3: Part1.D8, S3.Pin_1, S3.Pin_2
  N4: Part1.D9_PWM, S2.Pin_1, S2.Pin_2
  GND: Part1.GND, S1.Pin_3, S1.Pin_4, S2.Pin_3, S2.Pin_4, S3.Pin_3, S3.Pin_4, Part2.GND
  N5: Part1.D2, Part2.VCC
  N6: Part1.D7, S1.Pin_1, S1.Pin_2
  N7: Part1.5V, Part2.SEL

notes:
  Not real joystick, look at image in this folder; it has the same wire colours.
